// Logisim project cpu(2 pipelines).circ as structural Verilog: 1 circuit, main circuit cpu
module cpu (
  input  clk,
  input  [31:0] Instruction,
  input  [31:0] MemReadData,
  output [31:0] MemAddress,
  output [31:0] ProgramCounter,
  output [31:0] ra,
  output [31:0] sp,
  output [31:0] t0,
  output [31:0] t1,
  output [31:0] t2,
  output [31:0] s0,
  output [31:0] s1,
  output [31:0] a0,
  output [3:0] MemWriteMask,
  output [31:0] MemWriteData
);

  wire ASel, BrEq, BrLt, BrUn, BSel, MemWEn, partial_store_1_p5, partial_store_1_p6, partial_store_1_p8,
       partial_store_1_p10, PCSel, regfile_1_p7, regfile_1_p8, regfile_1_p10, regfile_1_p21, regfile_1_p23,
       RegWEn;
  wire [1:0] WBSel;
  wire [2:0] ImmSel;
  wire [3:0] ALUSel;
  wire [31:0] adder_1_out, adder_2_out, imm_gen_1_p4, Instruction_new, multiplexer_1_out, multiplexer_2_out,
       multiplexer_3_out, multiplexer_4_out, partial_load_1_p4, PC_new, ReadData1, ReadData2, WriteBack;

  Adder #(.width(32)) adder_1 (.a(ProgramCounter), .b(32'h4), .out(adder_1_out));  // open: cin, cout
  Register #(.width(32)) PC (.D(multiplexer_1_out), .clk(clk), .Q(ProgramCounter));  // open: en, clr
  Multiplexer #(.width(32)) multiplexer_1 (.in0(adder_1_out), .in1(MemAddress), .out(multiplexer_1_out), .sel(PCSel));
  Multiplexer #(.width(32)) multiplexer_2 (.in0(Instruction), .in1(32'h13), .out(multiplexer_2_out), .sel(PCSel));
  Register #(.width(32)) register_1 (.D(multiplexer_2_out), .clk(clk), .Q(Instruction_new));  // open: en, clr
  Register #(.width(32)) register_2 (.D(ProgramCounter), .clk(clk), .Q(PC_new));  // open: en, clr
  // control_logic control_logic_1: pin names not known; wires that end beside it: Instruction_new, PCSel, RegWEn, ImmSel, BrEq, BrLt
  // regfile regfile_1: pin names not known; wires that end beside it: Instruction_new[19:15], Instruction_new[24:20], Instruction_new[11:7], WriteBack, RegWEn, clk, regfile_1_p7, regfile_1_p8, regfile_1_p8, regfile_1_p10, ra, sp, t0, t1, t2, s0, s1, a0, ReadData1, regfile_1_p10, regfile_1_p21, regfile_1_p21, regfile_1_p23, regfile_1_p23
  // imm_gen imm_gen_1: pin names not known; wires that end beside it: Instruction_new, ImmSel, ReadData2, imm_gen_1_p4
  Multiplexer #(.width(32)) multiplexer_3 (.in0(ReadData2), .in1(imm_gen_1_p4), .out(multiplexer_3_out), .sel(BSel));
  Multiplexer #(.width(32)) multiplexer_4 (.in0(ReadData1), .in1(PC_new), .out(multiplexer_4_out), .sel(ASel));
  // alu alu_1: pin names not known; wires that end beside it: multiplexer_4_out, multiplexer_3_out, ALUSel, MemAddress
  // branch_comp branch_comp_1: pin names not known; wires that end beside it: ReadData1, ReadData2, BrUn, BrEq, BrLt
  // partial_store partial_store_1: pin names not known; wires that end beside it: Instruction_new, MemAddress, ReadData2, MemWEn, partial_store_1_p5, partial_store_1_p6, partial_store_1_p6, partial_store_1_p8, partial_store_1_p8, partial_store_1_p10, MemWriteMask, MemWriteData, partial_store_1_p5, partial_store_1_p10
  // partial_load partial_load_1: pin names not known; wires that end beside it: Instruction_new, MemAddress, MemReadData, partial_load_1_p4
  Adder #(.width(32)) adder_2 (.a(PC_new), .b(32'h4), .out(adder_2_out));  // open: cin, cout
  Multiplexer #(.select(2), .width(32)) multiplexer_5 (
    .in0(partial_load_1_p4), .in1(MemAddress), .in2(adder_2_out), .out(WriteBack), .sel(WBSel));  // open: in3

  // Other names for the same wires on the sheet: WriteData[31:0] = MemAddress

  // Notes on the sheet:
  //   To IMEM
  //   IMEM (do **NOT** move this)
  //   From IMEM
  //   Inputs/Outputs for testing. Do **NOT** move these.
  //   It is OK to move the PC, RegFile, ALU, MEM, Branch Comp, Imm Gen, Partial Load, Partial Store and Control Logic to wherever is most convenient for you when constructing your CPU, and to delete this text
  //   To DMEM
  //   DMEM (do **NOT** move this)
  //   From DMEM
endmodule
