// Logisim project cpu(5 pipelines).circ as structural Verilog: 1 circuit, main circuit cpu
module cpu (
  input  clk,
  input  [31:0] Instruction,
  input  [31:0] MemReadData,
  output [31:0] MemAddress,
  output [31:0] ProgramCounter,
  output [31:0] ra,
  output [31:0] sp,
  output [31:0] t0,
  output [31:0] t1,
  output [31:0] t2,
  output [31:0] s0,
  output [31:0] s1,
  output [31:0] a0,
  output [3:0] MemWriteMask,
  output [31:0] MemWriteData
);

  wire ASel, ASel1, BrEq, BrLt, BrUn, BrUn1, BSel, BSel1, MemWEn, MemWEn1, partial_store_1_p5,
       partial_store_1_p6, partial_store_1_p8, partial_store_1_p10, PCSel, regfile_1_p6, regfile_1_p7,
       regfile_1_p9, regfile_1_p22, regfile_1_p24, register_9_q, register_10_q, register_19_q, RegWEn,
       RegWEn1;
  wire [1:0] register_11_q, register_16_q, WBSel, WBSel1;
  wire [2:0] funct3, ImmSel;
  wire [3:0] ALUSel, ALUSel1;
  wire [4:0] rdfinal, register_2_q, register_3_q;
  wire [6:0] funct7;
  wire [24:0] Instruction_t;
  wire [31:0] adder_2_out, alu_1_p4, DataToReg, imm, imm_gen_1_p3, Instruction4, multiplexer_1_out,
       multiplexer_2_out, multiplexer_3_out, multiplexer_4_out, PCplus4, ProgramCounter3, ProgramCounter5,
       r1, r2, r22, regfile_1_p18, regfile_1_p19, register_7_q, register_8_q, register_25_q, register_28_q,
       register_29_q, WB;

  Adder #(.width(32)) adder_1 (.a(ProgramCounter), .b(32'h4), .out(PCplus4));  // open: cin, cout
  Multiplexer #(.width(32)) multiplexer_1 (.in0(PCplus4), .in1(MemAddress), .out(multiplexer_1_out), .sel(PCSel));
  Register #(.width(32)) register_1 (.D(multiplexer_1_out), .clk(clk), .Q(ProgramCounter));  // open: en, clr
  Register #(.width(5)) register_2 (.D(Instruction_t[11:7]), .clk(clk), .Q(register_2_q));  // open: en, clr
  Register #(.width(5)) register_3 (.D(register_2_q), .clk(clk), .Q(register_3_q));  // open: en, clr
  Multiplexer #(.width(32)) multiplexer_2 (.in0(Instruction), .in1(32'h13), .out(multiplexer_2_out), .sel(PCSel));
  Register #(.width(32)) register_4 (
    .D(multiplexer_2_out), .clk(clk), .Q({funct7, Instruction_t[24:15], funct3, Instruction_t[11:0]}));  // open: en, clr
  Register #(.width(32)) register_5 (.D(imm_gen_1_p3), .clk(clk), .Q(imm));  // open: en, clr
  // imm_gen imm_gen_1: pin names not known; wires that end beside it: {funct7, Instruction_t[24:15], funct3, Instruction_t[11:0]}, ImmSel, imm_gen_1_p3, clk
  Register #(.width(5)) register_6 (.D(register_3_q), .clk(clk), .Q(rdfinal));  // open: en, clr
  Register #(.width(32)) register_7 (.D(ProgramCounter), .clk(clk), .Q(register_7_q));  // open: en, clr
  Register #(.width(32)) register_8 (.D(ProgramCounter3), .clk(clk), .Q(register_8_q));  // open: en, clr
  Register #(.width(1)) register_9 (.D(RegWEn1), .clk(clk), .Q(register_9_q));  // open: en, clr
  Register #(.width(1)) register_10 (.D(MemWEn1), .clk(clk), .Q(register_10_q));  // open: en, clr
  Register #(.width(2)) register_11 (.D(WBSel1), .clk(clk), .Q(register_11_q));  // open: en, clr
  Register #(.width(32)) register_12 (.D(register_7_q), .clk(clk), .Q(ProgramCounter3));  // open: en, clr
  Register #(.width(4)) register_13 (.D(ALUSel1), .clk(clk), .Q(ALUSel));  // open: en, clr
  Register #(.width(1)) register_14 (.D(BrUn1), .clk(clk), .Q(BrUn));  // open: en, clr
  Register #(.width(1)) register_15 (.D(register_10_q), .clk(clk), .Q(MemWEn1));  // open: en, clr
  Register #(.width(2)) register_16 (.D(register_11_q), .clk(clk), .Q(register_16_q));  // open: en, clr
  // regfile regfile_1: pin names not known; wires that end beside it: Instruction_t[19:15], Instruction_t[24:20], rdfinal, WB, RegWEn, regfile_1_p6, regfile_1_p7, regfile_1_p7, regfile_1_p9, ra, sp, t0, t1, t2, s0, s1, a0, regfile_1_p18, regfile_1_p19, regfile_1_p9, clk, regfile_1_p22, regfile_1_p22, regfile_1_p24, regfile_1_p24
  Register #(.width(32)) register_17 (.D(regfile_1_p18), .clk(clk), .Q(r1));  // open: en, clr
  Register #(.width(32)) register_18 (.D(regfile_1_p19), .clk(clk), .Q(r2));  // open: en, clr
  Adder #(.width(32)) adder_2 (.a(register_8_q), .b(32'h4), .out(adder_2_out));  // open: cin, cout
  Register #(.width(1)) register_19 (.D(register_9_q), .clk(clk), .Q(register_19_q));  // open: en, clr
  Register #(.width(1)) register_20 (.D(ASel1), .clk(clk), .Q(ASel));  // open: en, clr
  Register #(.width(1)) register_21 (.D(BSel1), .clk(clk), .Q(BSel));  // open: en, clr
  Register #(.width(2)) register_22 (.D(register_16_q), .clk(clk), .Q(WBSel));  // open: en, clr
  Register #(.width(32)) register_23 (.D(adder_2_out), .clk(clk), .Q(ProgramCounter5));  // open: en, clr
  Register #(.width(1)) register_24 (.D(register_19_q), .clk(clk), .Q(RegWEn));  // open: en, clr
  Register #(.width(32)) register_25 (
    .D({funct7, Instruction_t[24:15], funct3, Instruction_t[11:0]}), .clk(clk), .Q(register_25_q));  // open: en, clr
  Multiplexer #(.width(32)) multiplexer_3 (.in0(r1), .in1(ProgramCounter3), .out(multiplexer_3_out), .sel(ASel));
  Multiplexer #(.width(32)) multiplexer_4 (.in0(r2), .in1(imm), .out(multiplexer_4_out), .sel(BSel));
  Register #(.width(32)) register_26 (.D(register_25_q), .clk(clk), .Q(Instruction4));  // open: en, clr
  // branch_comp branch_comp_1: pin names not known; wires that end beside it: r1, r2, BrUn, BrEq, BrLt
  // alu alu_1: pin names not known; wires that end beside it: multiplexer_3_out, multiplexer_4_out, ALUSel, alu_1_p4
  // control_logic control_logic_1: pin names not known; wires that end beside it: {funct7, Instruction_t[24:15], funct3, Instruction_t[11:0]}, PCSel, RegWEn1, ImmSel, BrEq, BrLt
  Register #(.width(32)) register_27 (.D(alu_1_p4), .clk(clk), .Q(MemAddress));  // open: en, clr
  Register #(.width(32)) register_28 (.D(MemAddress), .clk(clk), .Q(register_28_q));  // open: en, clr
  Register #(.width(32)) register_29 (.D(DataToReg), .clk(clk), .Q(register_29_q));  // open: en, clr
  Multiplexer #(.select(2), .width(32)) multiplexer_5 (
    .in0(register_29_q), .in1(register_28_q), .in2(ProgramCounter5), .out(WB), .sel(WBSel));  // open: in3
  // partial_store partial_store_1: pin names not known; wires that end beside it: Instruction4, MemAddress, r22, MemWEn, partial_store_1_p5, partial_store_1_p6, partial_store_1_p6, partial_store_1_p8, partial_store_1_p8, partial_store_1_p10, MemWriteMask, MemWriteData, partial_store_1_p5, partial_store_1_p10
  // partial_load partial_load_1: pin names not known; wires that end beside it: Instruction4, MemAddress, MemReadData, DataToReg
  Register #(.width(32)) register_30 (.D(r2), .clk(clk), .Q(r22));  // open: en, clr

  // Other names for the same wires on the sheet: ALUoutput[31:0] = MemAddress; opcode[6:0] = Instruction_t[6:0];
  //   rd[4:0] = Instruction_t[11:7]; Instruction_t (some bits) = {funct7, funct3}; rs1[4:0] = Instruction_t[19:15];
  //   rs2[4:0] = Instruction_t[24:20]; ProgramCounter1[31:0] = ProgramCounter

  // Notes on the sheet:
  //   To IMEM
  //   IMEM (do **NOT** move this)
  //   From IMEM
  //   Inputs/Outputs for testing. Do **NOT** move these.
  //   It is OK to move the PC, RegFile, ALU, MEM, Branch Comp, Imm Gen, Partial Load, Partial Store and Control Logic to wherever is most convenient for you when constructing your CPU, and to delete this text
  //   To DMEM
  //   DMEM (do **NOT** move this)
  //   From DMEM
endmodule
